// Logisim project as3.circ as structural Verilog: 12 circuits, main circuit main
module main (
  input  CarryIn,
  input  [1:0] Addr,
  input  Clock,
  input  [1:0] S_A,
  input  [1:0] S_B,
  input  ENA,
  input  ENB,
  input  [2:0] F2F1F0,
  input  [1:0] Selector,
  output Carry_out
);

  wire n2bdec_1_sel0, n2bdec_1_sel1, n2bdec_1_sel2, n2bdec_1_sel3, or_2_out;
  wire [1:0] MAR_out;
  wire [3:0] MDR_out, n4b_alu_1_output, n4bx1_multi_1_out, n4bx1_multi_2_out, or_1_out, R0_out, R1_out,
       R2_out;

  _2BDec u_2bdec_1 (
    .in0(Selector), .Sel0(n2bdec_1_sel0), .Sel1(n2bdec_1_sel1), .Sel2(n2bdec_1_sel2), .Sel3(n2bdec_1_sel3));
  assign or_1_out = n4b_alu_1_output;  // OR_Gate or_1, 4 bits wide OR_Gate
  buf or_2 (or_2_out, n2bdec_1_sel3);  // OR_Gate
  _2Bregister MAR (.In(Addr), .Clock(Clock), .Out(MAR_out));
  _4B_register MDR (.In(or_1_out), .Enable(or_2_out), .Clock(Clock), .Out(MDR_out));
  _4B_register R0 (.Enable(n2bdec_1_sel2), .Clock(Clock), .Out(R0_out));  // open: In
  _4B_register R1 (.Enable(n2bdec_1_sel1), .Clock(Clock), .Out(R1_out));  // open: In
  _4B_register R2 (.Enable(n2bdec_1_sel0), .Clock(Clock), .Out(R2_out));  // open: In
  _4Bx1_Multi u_4bx1_multi_1 (
    .Select(S_A), .In_0(MDR_out), .In_1(R0_out), .In_2(R1_out), .In_3(R2_out), .Out(n4bx1_multi_1_out));
  _4B_ALU u_4b_alu_1 (
    .A(n4bx1_multi_1_out), .B(n4bx1_multi_2_out), .CarryIn(CarryIn), .ENA(ENA), .ENB(ENB),
    .Output(n4b_alu_1_output), .Carry_Out(Carry_out), .F2F1F0(F2F1F0));
  _4Bx1_Multi u_4bx1_multi_2 (
    .Select(S_B), .In_0(MDR_out), .In_1(R0_out), .In_2(R1_out), .In_3(R2_out), .Out(n4bx1_multi_2_out));
  _4x4_Mem u_4x4_mem_1 (.LoadData(MDR_out), .Addr(MAR_out), .Clock(Clock));  // open: Select, R_W, output
endmodule

module DLatch (
  input  D,
  input  E,
  output Q_prime,
  output Q
);

  wire and_1_out, and_2_out, not_1_out;

  not not_1 (not_1_out, D);
  and and_1 (and_1_out, D, E);
  and and_2 (and_2_out, E, not_1_out);
  nor nor_1 (Q_prime, and_1_out, Q);
  nor nor_2 (Q, Q_prime, and_2_out);

  // Notes on the sheet:
  //   Q: pull=down
  //   E: pull=down
  //   Q_prime: pull=down
  //   D: pull=down
endmodule

// FF
module risingFlipFlop (
  input  D,
  input  C,
  output Q
);

  wire dlatch_1_q, not_1_out;

  DLatch dlatch_1 (.D(D), .E(not_1_out), .Q(dlatch_1_q));  // open: Q_prime
  not not_1 (not_1_out, C);
  DLatch dlatch_2 (.D(dlatch_1_q), .E(C), .Q(Q));  // open: Q_prime
endmodule

module _4B_register (
  input  [3:0] In,
  input  Enable,
  input  Clock,
  output [3:0] Out
);

  wire and_1_out;

  and and_1 (and_1_out, Enable, Clock);
  risingFlipFlop risingflipflop_1 (.D(In[0]), .C(and_1_out), .Q(Out[0]));
  risingFlipFlop risingflipflop_2 (.D(In[1]), .C(and_1_out), .Q(Out[1]));
  risingFlipFlop risingflipflop_3 (.D(In[2]), .C(and_1_out), .Q(Out[2]));
  risingFlipFlop risingflipflop_4 (.D(In[3]), .C(and_1_out), .Q(Out[3]));
endmodule

module _2BDec (
  input  [1:0] in0,
  output Sel0,
  output Sel1,
  output Sel2,
  output Sel3
);

  wire not_1_out, not_2_out;

  not not_1 (not_1_out, in0[0]);
  not not_2 (not_2_out, in0[1]);
  and and_1 (Sel0, not_1_out, not_2_out);
  and and_2 (Sel1, in0[0], not_2_out);
  and and_3 (Sel2, in0[1], not_1_out);
  and and_4 (Sel3, in0[0], in0[1]);

  // Notes on the sheet:
  //   in0: pull=down
endmodule

// Act
module _4B_Activator (
  input  Enable,
  input  [3:0] In,
  output [3:0] Out
);

  and and_1 (Out[0], In[0], Enable);
  and and_2 (Out[1], In[1], Enable);
  and and_3 (Out[2], In[2], Enable);
  and and_4 (Out[3], In[3], Enable);

  // Notes on the sheet:
  //   Enable: pull=down
endmodule

module _4Bx1_Multi (
  input  [1:0] Select,
  input  [3:0] In_0,
  input  [3:0] In_1,
  input  [3:0] In_2,
  input  [3:0] In_3,
  output [3:0] Out
);

  wire n2bdec_1_sel0, n2bdec_1_sel1, n2bdec_1_sel2, n2bdec_1_sel3;
  wire [3:0] n4b_activator_1_out, n4b_activator_2_out, n4b_activator_3_out, n4b_activator_4_out;

  _2BDec u_2bdec_1 (
    .in0(Select), .Sel0(n2bdec_1_sel0), .Sel1(n2bdec_1_sel1), .Sel2(n2bdec_1_sel2), .Sel3(n2bdec_1_sel3));
  _4B_Activator u_4b_activator_1 (.In(In_0), .Enable(n2bdec_1_sel0), .Out(n4b_activator_1_out));
  _4B_Activator u_4b_activator_2 (.In(In_1), .Enable(n2bdec_1_sel1), .Out(n4b_activator_2_out));
  _4B_Activator u_4b_activator_3 (.In(In_2), .Enable(n2bdec_1_sel2), .Out(n4b_activator_3_out));
  _4B_Activator u_4b_activator_4 (.In(In_3), .Enable(n2bdec_1_sel3), .Out(n4b_activator_4_out));
  assign Out = n4b_activator_1_out | n4b_activator_2_out | n4b_activator_3_out | n4b_activator_4_out;  // OR_Gate or_1, 4 bits wide
endmodule

module _2Bregister (
  input  [1:0] In,
  input  Clock,
  output [1:0] Out
);

  risingFlipFlop risingflipflop_1 (.D(In[0]), .C(Clock), .Q(Out[0]));
  risingFlipFlop risingflipflop_2 (.D(In[1]), .C(Clock), .Q(Out[1]));
endmodule

module _1B_ALU (
  input  CarryIn,
  input  A,
  input  ENA,
  input  B,
  input  ENB,
  input  F2,
  input  F1,
  input  F0,
  output aluOUT,
  output CarryOut
);

  wire and_1_out, and_2_out, and_3_out, and_4_out, and_5_out, and_6_out, and_7_out, and_8_out, and_9_out,
       and_10_out, n3to8b_decoder_1_sel000, n3to8b_decoder_1_sel001, n3to8b_decoder_1_sel010,
       n3to8b_decoder_1_sel011, n3to8b_decoder_1_sel100, not_1_out, not_2_out, or_1_out, xor_1_out, xor_2_out;

  and and_1 (and_1_out, A, ENA);
  and and_2 (and_2_out, B, ENB);
  _3to8B_Decoder u_3to8b_decoder_1 (
    .F3(F2), .F1(F1), .F0(F0), .Sel000(n3to8b_decoder_1_sel000), .Sel001(n3to8b_decoder_1_sel001),
    .Sel010(n3to8b_decoder_1_sel010), .Sel011(n3to8b_decoder_1_sel011), .Sel100(n3to8b_decoder_1_sel100));  // open: Sel101, Sel110, Sel111
  and and_3 (and_3_out, and_1_out, and_2_out);
  or or_1 (or_1_out, and_1_out, and_2_out);
  not not_1 (not_1_out, and_2_out);
  not not_2 (not_2_out, and_1_out);
  and and_4 (and_4_out, and_3_out, n3to8b_decoder_1_sel000);
  and and_5 (and_5_out, or_1_out, n3to8b_decoder_1_sel001);
  and and_6 (and_6_out, not_1_out, n3to8b_decoder_1_sel010);
  and and_7 (and_7_out, not_2_out, n3to8b_decoder_1_sel100);
  and and_8 (and_8_out, n3to8b_decoder_1_sel011, and_1_out, and_2_out);
  xor xor_1 (xor_1_out, and_2_out, and_1_out);
  or or_2 (CarryOut, and_8_out, and_9_out);
  and and_9 (and_9_out, n3to8b_decoder_1_sel011, xor_1_out, CarryIn);
  xor xor_2 (xor_2_out, CarryIn, xor_1_out);
  and and_10 (and_10_out, xor_2_out, n3to8b_decoder_1_sel011);
  or or_3 (aluOUT, and_4_out, and_5_out, and_7_out, and_6_out, and_10_out);

  // Notes on the sheet:
  //   Decoder (only use 000, 001, 010, 011, 100)
  //   Logic Unit
  //   Full Adder
  //   Limitations: I only implemented 5 functions
endmodule

// 3-8B-Dec
module _3to8B_Decoder (
  input  F3,
  input  F1,
  input  F0,
  output Sel000,
  output Sel001,
  output Sel010,
  output Sel011,
  output Sel100,
  output Sel101,
  output Sel110,
  output Sel111
);

  wire not_1_out, not_2_out, not_3_out;

  not not_1 (not_1_out, F3);
  not not_2 (not_2_out, F1);
  not not_3 (not_3_out, F0);
  and and_1 (Sel000, not_3_out, not_2_out, not_1_out);
  and and_2 (Sel001, F0, not_2_out, not_1_out);
  and and_3 (Sel010, not_3_out, F1, not_1_out);
  and and_4 (Sel011, F0, F1, not_1_out);
  and and_5 (Sel100, not_3_out, not_2_out, F3);
  and and_6 (Sel101, F0, not_2_out, F3);
  and and_7 (Sel110, not_3_out, F1, F3);
  and and_8 (Sel111, F0, F1, F3);
endmodule

module _4B_ALU (
  input  [3:0] A,
  input  [3:0] B,
  input  CarryIn,
  input  ENA,
  input  ENB,
  input  [2:0] F2F1F0,
  output [3:0] Output,
  output Carry_Out
);

  wire n1b_alu_1_carryout, n1b_alu_2_carryout, n1b_alu_3_carryout;

  _1B_ALU u_1b_alu_1 (
    .A(A[0]), .B(B[0]), .aluOUT(Output[0]), .CarryOut(n1b_alu_1_carryout), .CarryIn(CarryIn), .F2(F2F1F0[2]),
    .F1(F2F1F0[1]), .F0(F2F1F0[0]), .ENA(ENA), .ENB(ENB));
  _1B_ALU u_1b_alu_2 (
    .A(A[1]), .B(B[1]), .aluOUT(Output[1]), .CarryOut(n1b_alu_2_carryout), .CarryIn(n1b_alu_1_carryout),
    .F2(F2F1F0[2]), .F1(F2F1F0[1]), .F0(F2F1F0[0]), .ENA(ENA), .ENB(ENB));
  _1B_ALU u_1b_alu_3 (
    .A(A[2]), .B(B[2]), .aluOUT(Output[2]), .CarryOut(n1b_alu_3_carryout), .CarryIn(n1b_alu_2_carryout),
    .F2(F2F1F0[2]), .F1(F2F1F0[1]), .F0(F2F1F0[0]), .ENA(ENA), .ENB(ENB));
  _1B_ALU u_1b_alu_4 (
    .A(A[3]), .B(B[3]), .aluOUT(Output[3]), .CarryOut(Carry_Out), .CarryIn(n1b_alu_3_carryout),
    .F2(F2F1F0[2]), .F1(F2F1F0[1]), .F0(F2F1F0[0]), .ENA(ENA), .ENB(ENB));
endmodule

// Mem
module _4x4_Mem (
  input  [3:0] LoadData,
  input  [1:0] Addr,
  input  [3:0] \output ,
  input  Select,
  input  R_W,
  input  Clock
);

  wire and_1_out, and_2_out, and_3_out, and_4_out, and_6_out, and_7_out, and_8_out, and_9_out, and_10_out,
       and_11_out, and_12_out, and_13_out, n4b_register_1_p3, n4b_register_5_p3, n4b_register_9_p3,
       not_1_out, not_2_out, not_3_out, not_4_out, not_5_out, undriven;
  wire [3:0] and_14_out, n4b_register_13_out, n4b_register_14_out, n4b_register_15_out, n4b_register_16_out;

  not not_1 (not_1_out, Addr[0]);
  not not_2 (not_2_out, Addr[1]);
  not not_3 (not_3_out, Addr[0]);
  not not_4 (not_4_out, Addr[1]);
  and and_1 (and_1_out, not_1_out, not_2_out);
  and and_2 (and_2_out, not_3_out, Addr[1]);
  and and_3 (and_3_out, Addr[0], not_4_out);
  and and_4 (and_4_out, Addr[1], Addr[0]);
  and and_5 (and_4_out, Select, not_5_out);
  not not_5 (not_5_out, R_W);
  and and_6 (and_6_out, Select, R_W, Clock);
  and and_7 (and_7_out, and_4_out, and_1_out);
  and and_8 (and_8_out, and_4_out, and_2_out);
  and and_9 (and_9_out, and_4_out, and_3_out);
  and and_10 (and_10_out, and_4_out, and_4_out);
  // _4B_register 4b_register_1: pin names not known; wires that end beside it: LoadData, and_7_out, n4b_register_1_p3
  _4B_register u_4b_register_2 (.In(LoadData), .Clock(and_8_out));  // open: Enable, Out
  _4B_register u_4b_register_3 (.In(LoadData), .Clock(and_9_out));  // open: Enable, Out
  _4B_register u_4b_register_4 (.In(LoadData), .Clock(and_10_out));  // open: Enable, Out
  buf or_1 (and_6_out, and_11_out);  // OR_Gate
  and and_11 (and_11_out, and_1_out, n4b_register_1_p3);
  // _4B_register 4b_register_5: pin names not known; wires that end beside it: LoadData, and_7_out, n4b_register_5_p3
  _4B_register u_4b_register_6 (.In(LoadData), .Clock(and_8_out));  // open: Enable, Out
  _4B_register u_4b_register_7 (.In(LoadData), .Clock(and_9_out));  // open: Enable, Out
  _4B_register u_4b_register_8 (.In(LoadData), .Clock(and_10_out));  // open: Enable, Out
  buf or_2 (and_6_out, and_12_out);  // OR_Gate
  and and_12 (and_12_out, and_1_out, n4b_register_5_p3);
  // _4B_register 4b_register_9: pin names not known; wires that end beside it: LoadData, and_7_out, n4b_register_9_p3
  and and_13 (and_13_out, and_1_out, n4b_register_9_p3);
  _4B_register u_4b_register_10 (.In(LoadData), .Clock(and_8_out));  // open: Enable, Out
  _4B_register u_4b_register_11 (.In(LoadData), .Clock(and_9_out));  // open: Enable, Out
  _4B_register u_4b_register_12 (.In(LoadData), .Clock(and_10_out));  // open: Enable, Out
  buf or_3 (and_6_out, and_13_out);  // OR_Gate
  _4B_register u_4b_register_13 (.In(LoadData), .Clock(and_7_out), .Out(n4b_register_13_out));  // open: Enable
  _4B_register u_4b_register_14 (.In(LoadData), .Clock(and_8_out), .Out(n4b_register_14_out));  // open: Enable
  _4B_register u_4b_register_15 (.In(LoadData), .Clock(and_9_out), .Out(n4b_register_15_out));  // open: Enable
  _4B_register u_4b_register_16 (.In(LoadData), .Clock(and_10_out), .Out(n4b_register_16_out));  // open: Enable
  buf or_4 (and_6_out, undriven);  // OR_Gate
  assign and_14_out = n4b_register_16_out;  // AND_Gate and_14, 4 bits wide AND_Gate
  not not_6 (\output [0], and_6_out);
  not not_7 (\output [1], and_6_out);
  not not_8 (\output [2], and_6_out);
  not not_9 (\output [3], and_6_out);
  // AND_Gate and_15 has open pins: in0=n4b_register_13_out, out=open
  // AND_Gate and_16 has open pins: in0=n4b_register_14_out, out=open
  // AND_Gate and_17 has open pins: in0=n4b_register_15_out, out=open
endmodule
